# Fritzing sketch Untitled Sketch (saved by Fritzing 0.9.2b)
breadboards: 1

parts:
  Part1 = Arduino Uno (Rev3)
  LCD1 = LCD screen
  LED1 = smd LED [color="Red (633nm)" package="0805 [SMD]"]
  LED2 = smd LED [color="Red (633nm)" package="0805 [SMD]"]
  R1 = Resistor [tolerance=±5% resistance=220 package="2010 [SMD]"]
  R2 = Resistor [tolerance=±5% resistance=220 package="2010 [SMD]"]
  R3 = Rotary Potentiometer (Large) [maximum_resistance=100kΩ package=THT]
  SPKR1 = Loudspeaker
  J1 = Basic Servo
  KEYPAD1 = Membrane Matrix Keypad

nets:
  N1: Part1.A0, KEYPAD1.5
  N2: Part1.A1, KEYPAD1.6
  N3: Part1.A2, KEYPAD1.7
  N4: Part1.A3, SPKR1.pin2
  N5: Part1.A4/SDA, J1.pulse
  N6: Part1.A5/SCL, R1.Pin_0
  N7: Part1.D8, LCD1.DB5
  N8: Part1.D9_PWM, LCD1.DB4
  N9: Part1.D10_PWM/SS, LCD1.E
  N10: Part1.D12/MISO, LCD1.RS
  N11: Part1.D13/SCK, R2.Pin_0
  N12: Part1.D2, KEYPAD1.4
  N13: Part1.D3_PWM, KEYPAD1.3
  N14: Part1.D4, KEYPAD1.2
  N15: Part1.D5_PWM, KEYPAD1.1
  N16: Part1.D6_PWM, LCD1.DB7
  N17: Part1.D7, LCD1.DB6
  5V: Part1.5V, LCD1.VDD, LCD1.LED+, R3.leg2, J1.vcc
  GND: Part1.GND, LCD1.VSS, LCD1.LED-, LED1.cathode, LED2.cathode, R3.leg1, SPKR1.pin1, J1.gnd
  N18: LCD1.V0, R3.wiper
  N19: LED1.anode, R1.Pin_1
  N20: LED2.anode, R2.Pin_1

custom parts:
  Membrane Matrix Keypad: Membrane Matrix 3x4 Keypad
